// Logisim project curcuit.circ as structural Verilog: 10 circuits, main circuit main
module main (
);

  wire clck, clock_1_out, dipswitch_1_sw1, HLT, reset;

  and and_1 (clck, clock_1_out, dipswitch_1_sw1);
  Clock clock_1 (.out(clock_1_out));
  DipSwitch #(.number(2)) dipswitch_1 (.sw1(dipswitch_1_sw1), .sw2(HLT));
  CPU cpu_1 (.reset(reset), .Clock(clck));
  Button R (.out(reset));
endmodule

module ProgramCounter (
  input  [31:0] JmpAddr,
  input  Reset,
  input  Jmp,
  input  Clock,
  output [31:0] ip
);

  wire [31:0] adder_1_out, multiplexer_1_out;

  Adder #(.width(32)) adder_1 (.a(ip), .b(32'h1), .out(adder_1_out));  // open: cin, cout
  Multiplexer #(.width(32)) multiplexer_1 (.in0(adder_1_out), .in1(JmpAddr), .out(multiplexer_1_out), .sel(Jmp));
  Register #(.width(32)) PC (.D(multiplexer_1_out), .en(1'b1), .Q(ip), .clk(Clock), .clr(Reset));
endmodule

module CPU (
  input  reset,
  input  Clock
);

  wire ALU_Calc, executor_1_hlt, JMP, MI, ML, MO, PCUp, RDW, SR1O;
  wire [2:0] alu_1_co, flags;
  wire [3:0] ALU_OP, DRID, instrdecoder_1_dr, instrdecoder_1_sr1, instrdecoder_1_sr2, pla_1_out, SR1ID, SR2ID;
  wire [11:0] instrdecoder_1_nop;
  wire [23:0] bit_extender_1_out;
  wire [31:0] alu_1_a_o, cpu_bus, IRFD, MAR, PCI, PCO, ram_1_dout, SR1, SR2;

  Bit_Extender #(.in_width(32), .out_width(24), .\type ("zero")) bit_extender_1 (.in(MAR), .out(bit_extender_1_out));
  RAM #(.addrWidth(24), .dataWidth(32)) ram_1 (
    .addr(bit_extender_1_out), .we(MI), .oe(ML), .clk(Clock), .din(cpu_bus), .dout(ram_1_dout));
  RegisterBank registerbank_1 (
    .C(Clock), .R(reset), .W(RDW), .PCO(PCO), .RS1(SR1ID), .RS2(SR2ID), .DR(DRID), .DRD(cpu_bus), .PCI(PCI),
    .IRFD(IRFD), .MAR(MAR), .S1(SR1), .S2(SR2));
  ProgramCounter PC (.JmpAddr(PCI), .Reset(reset), .Jmp(JMP), .Clock(PCUp), .ip(PCO));
  Multiplexer #(.width(32)) multiplexer_1 (.in1(ram_1_dout), .out(cpu_bus), .sel(MO));  // open: in0
  Multiplexer #(.width(32)) multiplexer_2 (.in1(SR1), .out(cpu_bus), .sel(SR1O));  // open: in0
  InstrDecoder instrdecoder_1 (
    .IR(IRFD), .flags(flags), .ALUOP(ALU_OP), .DR(instrdecoder_1_dr), .SR2(instrdecoder_1_sr2),
    .SR1(instrdecoder_1_sr1), .NOP(instrdecoder_1_nop[0]), .ALUCalc(instrdecoder_1_nop[1]),
    .ALUComp(instrdecoder_1_nop[2]), .JMP(instrdecoder_1_nop[3]), .LD(instrdecoder_1_nop[4]),
    .LDF(instrdecoder_1_nop[5]), .LDI(instrdecoder_1_nop[6]), .error(instrdecoder_1_nop[7]),
    .ST(instrdecoder_1_nop[8]), .STT(instrdecoder_1_nop[9]), .MOV(instrdecoder_1_nop[10]),
    .IOC(instrdecoder_1_nop[11]));
  ALU alu_1 (
    .C_or_B(1'b0), .Op(ALU_OP), .N1(SR1), .N2(SR2), .MC({32{1'b0}}), .CO(alu_1_co[0]), .BO(alu_1_co[1]),
    .A_O(alu_1_a_o), .Comp(alu_1_co[2]));  // open: MCO
  PLA #(.in_width(12), .out_width(4), .\table ("000000000001 0000 # NOP\n000000000010 0001 # Calc\n000000000100 0010 # Comp\n000000001000 0011 # JMP\n000000010000 0100 # LD\n000000100000 0101 # LDF\n000001000000 0110 # LDI\n000010000000 0111 # Error\n000100000000 1000 # ST\n001000000000 0001 # STT\n010000000000 0000 # MOV\n100000000000 0000 # IOC")) pla_1 (
    .in(instrdecoder_1_nop), .out(pla_1_out));
  Multiplexer #(.width(32)) multiplexer_3 (.in1(alu_1_a_o), .out(cpu_bus), .sel(ALU_Calc));  // open: in0
  Register #(.width(3)) register_1 (.D(alu_1_co), .en(ALU_Calc), .clk(Clock), .Q(flags), .clr(reset));
  Executor executor_1 (
    .Clock(Clock), .OP(pla_1_out), .reset(reset), .SR1ID(instrdecoder_1_sr1), .SR2ID(instrdecoder_1_sr2),
    .DRID(instrdecoder_1_dr), .MI(MI), .ML(ML), .MO(MO), .SR1O(SR1O), .DRW(RDW), .ALUCalc(ALU_Calc),
    .JMP(JMP), .HLT(executor_1_hlt), .PCU(PCUp), .SR1IDO(SR1ID), .SR2IDO(SR2ID), .DRIDO(DRID));

  // Other names for the same wires on the sheet: clck = Clock
endmodule

module ALU (
  input  C_or_B,
  input  [3:0] Op,
  input  [31:0] N1,
  input  [31:0] N2,
  input  [31:0] MC,
  output CO,
  output BO,
  output [31:0] MCO,
  output [31:0] A_O,
  output Comp
);

  wire comparator_1_eq, comparator_1_gt, comparator_1_lt;
  wire [4:0] bit_extender_1_out, bit_extender_2_out, bit_extender_3_out, bit_extender_4_out,
       bit_extender_5_out;
  wire [31:0] adder_1_out, and_1_out, multiplier_1_out, nand_1_out, negator_1_out, not_1_out, or_1_out,
       shifter_1_out, shifter_2_out, shifter_3_out, shifter_4_out, shifter_5_out, subtractor_1_out,
       xnor_1_out, xor_1_out;

  Bit_Extender #(.in_width(32), .out_width(5), .\type ("zero")) bit_extender_1 (.in(N2), .out(bit_extender_1_out));
  Bit_Extender #(.in_width(32), .out_width(5), .\type ("zero")) bit_extender_2 (.in(N2), .out(bit_extender_2_out));
  Bit_Extender #(.in_width(32), .out_width(5), .\type ("zero")) bit_extender_3 (.in(N2), .out(bit_extender_3_out));
  Bit_Extender #(.in_width(32), .out_width(5), .\type ("zero")) bit_extender_4 (.in(N2), .out(bit_extender_4_out));
  Bit_Extender #(.in_width(32), .out_width(5), .\type ("zero")) bit_extender_5 (.in(N2), .out(bit_extender_5_out));
  Adder #(.width(32)) adder_1 (.a(N1), .b(N2), .out(adder_1_out), .cin(C_or_B), .cout(CO));
  Subtractor #(.width(32)) subtractor_1 (.a(N1), .b(N2), .out(subtractor_1_out), .bin(C_or_B), .bout(BO));
  Multiplier #(.width(32)) multiplier_1 (.a(N1), .b(N2), .out(multiplier_1_out), .cin(MC), .cout(MCO));
  Negator #(.width(32)) negator_1 (.in(N1), .out(negator_1_out));
  assign and_1_out = N1 & N2;  // AND_Gate and_1, 32 bits wide
  assign or_1_out = N1 | N2;  // OR_Gate or_1, 32 bits wide
  assign not_1_out = ~N1;  // NOT_Gate not_1, 32 bits wide
  assign nand_1_out = ~(N1 & N2);  // NAND_Gate nand_1, 32 bits wide
  assign xor_1_out = N1 ^ N2;  // XOR_Gate xor_1, 32 bits wide
  assign xnor_1_out = ~(N1 ^ N2);  // XNOR_Gate xnor_1, 32 bits wide
  Shifter #(.width(32)) shifter_1 (.in(N1), .\dist (bit_extender_1_out), .out(shifter_1_out));
  Shifter #(.shift("lr"), .width(32)) shifter_2 (.in(N1), .\dist (bit_extender_2_out), .out(shifter_2_out));
  Shifter #(.shift("ar"), .width(32)) shifter_3 (.in(N1), .\dist (bit_extender_3_out), .out(shifter_3_out));
  Shifter #(.shift("rl"), .width(32)) shifter_4 (.in(N1), .\dist (bit_extender_4_out), .out(shifter_4_out));
  Shifter #(.shift("rr"), .width(32)) shifter_5 (.in(N1), .\dist (bit_extender_5_out), .out(shifter_5_out));
  Comparator #(.mode("unsigned"), .width(32)) comparator_1 (
    .a(N1), .b(N2), .gt(comparator_1_gt), .eq(comparator_1_eq), .lt(comparator_1_lt));
  Multiplexer #(.select(4), .width(32)) multiplexer_1 (
    .in0(adder_1_out), .in1(subtractor_1_out), .in2(multiplier_1_out), .in3(negator_1_out), .in4(and_1_out),
    .in5(or_1_out), .in6(not_1_out), .in7(nand_1_out), .in8(xor_1_out), .in9(xnor_1_out),
    .in10(shifter_1_out), .in11(shifter_2_out), .in12(shifter_3_out), .in13(shifter_4_out),
    .in14(shifter_5_out), .in15({32{1'b0}}), .out(A_O), .sel(Op));
  Multiplexer #(.select(4)) multiplexer_2 (
    .in0(comparator_1_gt), .in1(comparator_1_eq), .in2(comparator_1_lt), .in3(1'b0), .in4(1'b0), .in5(1'b0),
    .in6(1'b0), .in7(1'b0), .in8(1'b0), .in9(1'b0), .in10(1'b0), .in11(1'b0), .in12(1'b0), .in13(1'b0),
    .in14(1'b0), .in15(1'b0), .out(Comp), .sel(Op));
endmodule

module RegisterBank (
  input  C,
  input  R,
  input  W,
  input  [31:0] PCO,
  input  [3:0] RS1,
  input  [3:0] RS2,
  input  [3:0] DR,
  input  [31:0] DRD,
  output [31:0] PCI,
  output [31:0] IRFD,
  output [31:0] MAR,
  output [31:0] S1,
  output [31:0] S2
);

  wire and_1_out, and_2_out, and_3_out, and_4_out, and_5_out, and_6_out, and_7_out, and_8_out, and_9_out,
       and_10_out, and_11_out, and_12_out, and_13_out, and_14_out, and_15_out, decoder_1_out1,
       decoder_1_out2, decoder_1_out3, decoder_1_out4, decoder_1_out5, decoder_1_out6, decoder_1_out7,
       decoder_1_out8, decoder_1_out9, decoder_1_out10, decoder_1_out11, decoder_1_out12, decoder_1_out13,
       decoder_1_out14, decoder_1_out15;
  wire [31:0] bit_extender_1_out, register_2_q, register_4_q, register_5_q, register_6_q, register_7_q,
       register_8_q, register_9_q, register_10_q, register_11_q, register_12_q, register_13_q, register_14_q,
       register_15_q;

  Decoder #(.enable("false"), .select(4)) decoder_1 (
    .out1(decoder_1_out1), .out2(decoder_1_out2), .out3(decoder_1_out3), .out4(decoder_1_out4),
    .out5(decoder_1_out5), .out6(decoder_1_out6), .out7(decoder_1_out7), .out8(decoder_1_out8),
    .out9(decoder_1_out9), .out10(decoder_1_out10), .out11(decoder_1_out11), .out12(decoder_1_out12),
    .out13(decoder_1_out13), .out14(decoder_1_out14), .out15(decoder_1_out15), .sel(DR));  // open: out0
  Register #(.width(32)) register_1 (
    .D(DRD), .en(and_1_out), .clk(C),
    .Q({IRFD[0], IRFD[1], IRFD[2], IRFD[3], IRFD[4], IRFD[5], IRFD[6], IRFD[7], IRFD[8], IRFD[9], IRFD[10], IRFD[11], IRFD[12], IRFD[13], IRFD[14], IRFD[15], IRFD[16], IRFD[17], IRFD[18], IRFD[19], IRFD[20], IRFD[21], IRFD[22], IRFD[23], IRFD[24], IRFD[25], IRFD[26], IRFD[27], IRFD[28], IRFD[29], IRFD[30], IRFD[31]}),
    .clr(R));
  and and_1 (and_1_out, decoder_1_out1, W);
  Register #(.width(32)) register_2 (.D(DRD), .en(and_2_out), .clk(C), .Q(register_2_q), .clr(R));
  and and_2 (and_2_out, decoder_1_out2, W);
  Register #(.width(32)) register_3 (.D(DRD), .en(and_3_out), .clk(C), .Q(MAR), .clr(R));
  and and_3 (and_3_out, decoder_1_out3, W);
  and and_4 (and_4_out, decoder_1_out4, W);
  and and_5 (and_5_out, decoder_1_out5, W);
  and and_6 (and_6_out, decoder_1_out6, W);
  Register #(.width(32)) register_4 (.D(DRD), .en(and_4_out), .clk(C), .Q(register_4_q), .clr(R));
  Register #(.width(32)) register_5 (.D(DRD), .en(and_5_out), .clk(C), .Q(register_5_q), .clr(R));
  Register #(.width(32)) register_6 (.D(DRD), .en(and_6_out), .clk(C), .Q(register_6_q), .clr(R));
  Register #(.width(32)) register_7 (.D(DRD), .en(and_7_out), .clk(C), .Q(register_7_q), .clr(R));
  and and_7 (and_7_out, decoder_1_out7, W);
  Register #(.width(32)) register_8 (.D(DRD), .en(and_8_out), .clk(C), .Q(register_8_q), .clr(R));
  and and_8 (and_8_out, decoder_1_out8, W);
  Register #(.width(32)) register_9 (.D(DRD), .en(and_9_out), .clk(C), .Q(register_9_q), .clr(R));
  and and_9 (and_9_out, decoder_1_out9, W);
  Register #(.width(32)) register_10 (.D(DRD), .en(and_10_out), .clk(C), .Q(register_10_q), .clr(R));
  and and_10 (and_10_out, decoder_1_out10, W);
  Register #(.width(32)) register_11 (.D(DRD), .en(and_11_out), .clk(C), .Q(register_11_q), .clr(R));
  and and_11 (and_11_out, decoder_1_out11, W);
  and and_12 (and_12_out, decoder_1_out12, W);
  and and_13 (and_13_out, decoder_1_out13, W);
  and and_14 (and_14_out, decoder_1_out14, W);
  Register #(.width(32)) register_12 (.D(DRD), .en(and_12_out), .clk(C), .Q(register_12_q), .clr(R));
  Register #(.width(32)) register_13 (.D(DRD), .en(and_13_out), .clk(C), .Q(register_13_q), .clr(R));
  Register #(.width(32)) register_14 (.D(DRD), .en(and_14_out), .clk(C), .Q(register_14_q), .clr(R));
  Register #(.width(32)) register_15 (.D(DRD), .en(and_15_out), .clk(C), .Q(register_15_q), .clr(R));
  and and_15 (and_15_out, decoder_1_out15, W);
  assign bit_extender_1_out = {{8{1'b0}}, IRFD[31:8]};  // Bit_Extender bit_extender_1
  Multiplexer #(.select(4), .width(32)) multiplexer_1 (
    .in0(PCO), .in1(bit_extender_1_out), .in2(register_2_q), .in3(MAR), .in4(register_4_q),
    .in5(register_5_q), .in6(register_6_q), .in7(register_7_q), .in8(register_8_q), .in9(register_9_q),
    .in10(register_10_q), .in11(register_11_q), .in12(register_12_q), .in13(register_13_q),
    .in14(register_14_q), .in15(register_15_q), .out(S1), .sel(RS1));
  Multiplexer #(.select(4), .width(32)) multiplexer_2 (
    .in1(bit_extender_1_out), .in2(register_2_q), .in3(MAR), .in4(register_4_q), .in5(register_5_q),
    .in6(register_6_q), .in7(register_7_q), .in8(register_8_q), .in9(register_9_q), .in10(register_10_q),
    .in11(register_11_q), .in12(register_12_q), .in13(register_13_q), .in14(register_14_q),
    .in15(register_15_q), .out(S2), .sel(RS2));  // open: in0

  assign PCI = DRD;
endmodule

module InstrDecoder (
  input  [31:0] IR,
  input  [2:0] flags,
  output [3:0] ALUOP,
  output [3:0] DR,
  output [3:0] SR2,
  output [3:0] SR1,
  output NOP,
  output ALUCalc,
  output ALUComp,
  output JMP,
  output LD,
  output LDF,
  output LDI,
  output error,
  output ST,
  output STT,
  output MOV,
  output IOC
);

  wire and_1_out, and_2_out, and_3_out, and_4_out, decoder_1_out0, decoder_1_out3, decoder_1_out11,
       decoder_1_out12, decoder_1_out13, decoder_1_out14, decoder_1_out15, not_1_out, not_2_out, not_3_out,
       not_4_out, not_5_out, or_1_out, or_3_out, or_4_out;
  wire [3:0] multiplexer_2_out, multiplexer_3_out, multiplexer_6_out;

  Decoder #(.enable("false"), .select(4)) decoder_1 (
    .out0(decoder_1_out0), .out1(ALUCalc), .out2(ALUComp), .out3(decoder_1_out3), .out4(LD), .out5(LDF),
    .out6(LDI), .out7(ST), .out8(STT), .out9(MOV), .out10(IOC), .out11(decoder_1_out11),
    .out12(decoder_1_out12), .out13(decoder_1_out13), .out14(decoder_1_out14), .out15(decoder_1_out15),
    .sel(IR[3:0]));
  Multiplexer #(.width(4)) multiplexer_1 (.in0(IR[19:16]), .in1(IR[15:12]), .out(ALUOP), .sel(ALUComp));
  Multiplexer #(.width(4)) multiplexer_2 (.in0(IR[15:12]), .in1(IR[7:4]), .out(multiplexer_2_out), .sel(LD));
  or or_1 (or_1_out, LD, ST);
  or or_2 (error, decoder_1_out11, decoder_1_out12, decoder_1_out13, decoder_1_out14, decoder_1_out15);
  Multiplexer #(.width(4)) multiplexer_3 (
    .in0(multiplexer_2_out), .in1(IR[7:4]), .out(multiplexer_3_out), .sel(or_3_out));
  Multiplexer #(.width(4)) multiplexer_4 (.in0(IR[11:8]), .in1(4'b0001), .out(SR2), .sel(or_1_out));
  or or_3 (or_3_out, LDI, LDF);
  Multiplexer #(.width(4)) multiplexer_5 (.in0(multiplexer_3_out), .in1(SR2), .out(DR), .sel(MOV));
  Multiplexer #(.width(4)) multiplexer_6 (.in0(IR[7:4]), .in1(4'b0001), .out(multiplexer_6_out), .sel(or_3_out));
  not not_1 (not_1_out, multiplexer_6_out[1]);
  not not_2 (not_2_out, multiplexer_6_out[0]);
  not not_3 (not_3_out, flags[0]);
  not not_4 (not_4_out, flags[2]);
  and and_1 (and_1_out, decoder_1_out3, not_1_out, multiplexer_6_out[0], not_3_out);
  and and_2 (and_2_out, decoder_1_out3, multiplexer_6_out[1], not_2_out, not_4_out);
  and and_3 (and_3_out, decoder_1_out3, multiplexer_6_out[1], multiplexer_6_out[0], flags[2]);
  Multiplexer #(.width(4)) multiplexer_7 (.in0(multiplexer_6_out), .in1(SR2), .out(SR1), .sel(decoder_1_out3));
  or or_4 (or_4_out, and_1_out, and_2_out, and_3_out);
  not not_5 (not_5_out, decoder_1_out3);
  and and_4 (and_4_out, decoder_1_out3, ~JMP);  // AND_Gate
  Multiplexer multiplexer_8 (.in0(decoder_1_out3), .in1(not_5_out), .out(JMP), .sel(or_4_out));
  or or_5 (NOP, and_4_out, decoder_1_out0);

  // Other names for the same wires on the sheet: carry = flags[0]; comp = flags[2]
endmodule

module Executor (
  input  Clock,
  input  [3:0] OP,
  input  reset,
  input  [3:0] SR1ID,
  input  [3:0] SR2ID,
  input  [3:0] DRID,
  output MI,
  output ML,
  output MO,
  output SR1O,
  output DRW,
  output ALUCalc,
  output JMP,
  output HLT,
  output PCU,
  output [3:0] SR1IDO,
  output [3:0] SR2IDO,
  output [3:0] DRIDO
);

  wire executor_ca_1_rsc, or_1_out;
  wire [1:0] executor_ca_1_pco_mai;
  wire [2:0] counter_3_bit_1_count;
  wire [3:0] register_1_q;

  Register #(.width(4)) register_1 (.D(OP), .en(Clock), .clk(Clock), .Q(register_1_q), .clr(reset));
  or or_1 (or_1_out, reset, executor_ca_1_rsc);
  counter_3_bit counter_3_bit_1 (.C(Clock), .R(or_1_out), .count(counter_3_bit_1_count));
  executor_CA executor_ca_1 (
    .OP(register_1_q), .SBC(counter_3_bit_1_count), .MI(MI), .ML(ML), .MO(MO), .SR1O(SR1O), .DRW(DRW),
    .ALUCalc(ALUCalc), .JMP(JMP), .HLT(HLT), .PCU(PCU), .RSC(executor_ca_1_rsc),
    .PCO_MAI(executor_ca_1_pco_mai[0]), .IRI(executor_ca_1_pco_mai[1]));
  Multiplexer #(.width(4)) multiplexer_1 (.in0(SR1ID), .in1(4'b0000), .out(SR1IDO), .sel(executor_ca_1_pco_mai[0]));
  Multiplexer #(.select(2), .width(4)) multiplexer_2 (
    .in0(DRID), .in1(4'b0011), .in2(4'b0001), .out(DRIDO), .sel(executor_ca_1_pco_mai));  // open: in3

  assign SR2IDO = SR2ID;
endmodule

module Fetch (
  input  C,
  input  En,
  output PCO,
  output MAI,
  output ML,
  output MO,
  output IRI,
  output Stall,
  output RSBC,
  output PCUP
);

  wire not_1_out;
  wire [2:0] counter_3_bit_1_count;

  not not_1 (not_1_out, En);
  PLA #(.in_width(3), .out_width(8), .\table ("000 00000000 # Do Nothing\n001 00100011\n010 10100100\n011 00111000\n100 01000000\n101 00100000\n110 00100000\n111 00100000")) pla_1 (
    .in(counter_3_bit_1_count), .out({PCUP, RSBC, Stall, IRI, MO, ML, MAI, PCO}));
  counter_3_bit counter_3_bit_1 (.C(C), .R(not_1_out), .count(counter_3_bit_1_count));
endmodule

module counter_3_bit (
  input  C,
  input  R,
  output [2:0] count
);

  wire j_k_ff_1_qn, j_k_ff_2_qn, j_k_ff_3_qn, not_1_out, not_2_out, not_3_out;

  J_K_Flip_Flop j_k_ff_1 (
    .J(j_k_ff_1_qn), .K(not_1_out), .clk(C), .Q(count[0]), .Qn(j_k_ff_1_qn), .reset(R));  // open: preset
  not not_1 (not_1_out, j_k_ff_1_qn);
  J_K_Flip_Flop j_k_ff_2 (
    .J(j_k_ff_2_qn), .K(not_2_out), .clk(j_k_ff_1_qn), .Q(count[1]), .Qn(j_k_ff_2_qn), .reset(R));  // open: preset
  not not_2 (not_2_out, j_k_ff_2_qn);
  J_K_Flip_Flop j_k_ff_3 (
    .J(j_k_ff_3_qn), .K(not_3_out), .clk(j_k_ff_2_qn), .Q(count[2]), .Qn(j_k_ff_3_qn), .reset(R));  // open: preset
  not not_3 (not_3_out, j_k_ff_3_qn);
endmodule

module executor_CA (
  input  [3:0] OP,
  input  [2:0] SBC,
  output MI,
  output ML,
  output MO,
  output SR1O,
  output DRW,
  output ALUCalc,
  output JMP,
  output HLT,
  output PCU,
  output RSC,
  output PCO_MAI,
  output IRI
);

  wire and_1_out, and_2_out, and_3_out, and_4_out, and_5_out, and_6_out, and_7_out, and_8_out, and_9_out,
       and_10_out, and_11_out, and_12_out, and_13_out, and_14_out, and_15_out, and_16_out, and_20_out,
       and_21_out, and_22_out, and_23_out, and_24_out, and_25_out, and_26_out, and_27_out, not_1_out,
       not_2_out, not_3_out, not_4_out, not_5_out, not_6_out, not_7_out;

  not not_1 (not_1_out, OP[3]);
  not not_2 (not_2_out, OP[2]);
  not not_3 (not_3_out, OP[1]);
  not not_4 (not_4_out, OP[0]);
  not not_5 (not_5_out, SBC[2]);
  not not_6 (not_6_out, SBC[1]);
  not not_7 (not_7_out, SBC[0]);
  and and_1 (and_1_out, OP[3], not_2_out, not_3_out, not_4_out, not_5_out, SBC[1], SBC[0]);
  and and_2 (and_2_out, not_1_out, OP[2], OP[1], OP[0], not_5_out, SBC[1], SBC[0]);
  and and_3 (and_3_out, not_5_out, not_6_out, SBC[0]);
  and and_4 (and_4_out, not_1_out, OP[2], not_3_out, not_5_out, SBC[0]);
  and and_5 (and_5_out, not_5_out, SBC[1], not_7_out);
  and and_6 (and_6_out, not_1_out, OP[2], not_3_out, SBC[2], not_6_out, not_7_out);
  and and_7 (and_7_out, not_5_out, not_6_out, not_7_out);
  and and_8 (and_8_out, OP[3], not_2_out, not_3_out, not_5_out, SBC[1], SBC[0]);
  and and_9 (and_9_out, not_1_out, OP[2], OP[1], not_5_out, SBC[1], SBC[0]);
  and and_10 (and_10_out, not_1_out, OP[1], OP[0], not_5_out, SBC[1], SBC[0]);
  and and_11 (and_11_out, not_5_out, not_7_out);
  and and_12 (and_12_out, not_2_out, not_3_out, OP[0], not_5_out, SBC[1]);
  and and_13 (and_13_out, not_1_out, OP[2], not_3_out, not_6_out, not_7_out);
  and and_14 (and_14_out, not_1_out, OP[2], OP[1], not_4_out, not_5_out, SBC[1]);
  and and_15 (and_15_out, not_1_out, not_2_out, OP[1], not_4_out, not_5_out, SBC[1], SBC[0]);
  and and_16 (and_16_out, not_1_out, not_2_out, not_3_out, OP[0], not_5_out, SBC[1], SBC[0]);
  and and_17 (JMP, not_1_out, not_2_out, OP[1], OP[0], not_5_out, SBC[1], SBC[0]);
  and and_18 (HLT, OP[3], OP[2], OP[1], OP[0], not_5_out, SBC[1], SBC[0]);
  and and_19 (PCU, not_5_out, not_6_out, SBC[0]);
  and and_20 (and_20_out, OP[3], not_2_out, not_3_out, SBC[2], not_6_out, not_7_out);
  and and_21 (and_21_out, not_1_out, OP[2], not_3_out, SBC[2], not_6_out, SBC[0]);
  and and_22 (and_22_out, not_1_out, not_2_out, not_3_out, not_4_out, SBC[2], SBC[1], SBC[0]);
  and and_23 (and_23_out, OP[3], OP[2], not_3_out, not_5_out, SBC[1], SBC[0]);
  and and_24 (and_24_out, not_1_out, OP[1], SBC[2], not_6_out, not_7_out);
  and and_25 (and_25_out, OP[3], not_2_out, OP[1], not_5_out, SBC[1], SBC[0]);
  and and_26 (and_26_out, not_1_out, not_2_out, OP[0], SBC[2], not_6_out, not_7_out);
  and and_27 (and_27_out, OP[3], OP[1], not_4_out, not_5_out, SBC[1], SBC[0]);
  and and_28 (PCO_MAI, not_5_out, not_6_out, not_7_out);
  and and_29 (IRI, not_5_out, SBC[1], not_7_out);
  or or_1 (MI, and_1_out, and_2_out);
  or or_2 (ML, and_3_out, and_4_out);
  or or_3 (MO, and_5_out, and_6_out);
  or or_4 (SR1O, and_7_out, and_8_out, and_9_out, and_10_out);
  or or_5 (DRW, and_11_out, and_12_out, and_13_out, and_14_out);
  or or_6 (ALUCalc, and_15_out, and_16_out);
  or or_7 (RSC, and_20_out, and_21_out, and_22_out, and_23_out, and_24_out, and_25_out, and_26_out, and_27_out);
endmodule
